// Logisim project XORTutorialStewartKeira.circ as structural Verilog: 1 circuit, main circuit main
module main (
  input  Not_Gate,
  input  in_2,
  output out_3
);

  wire and_1_out, and_2_out, not_1_out, not_2_out;

  not not_1 (not_1_out, Not_Gate);
  not not_2 (not_2_out, in_2);
  and and_1 (and_1_out, not_1_out, in_2);
  and and_2 (and_2_out, Not_Gate, not_2_out);
  or or_1 (out_3, and_1_out, and_2_out);

  // Notes on the sheet:
  //   Keira Stewart
  //   November 15, 2023
  //   Not Gate
  //   And Gate
  //   And Gate
  //   Or Gate
endmodule
